// Logisim project FPLA.circ as structural Verilog: 3 circuits, main circuit main
module main (
  input  Normal_Test,
  input  \config ,
  input  clk,
  input  reset
);

  wire demultiplexer_1_out0, demultiplexer_1_out1, demultiplexer_2_out0, demultiplexer_2_out1,
       demultiplexer_3_out0, demultiplexer_3_out1, demultiplexer_4_out0, demultiplexer_4_out1,
       multiplexer_1_out, multiplexer_2_out, multiplexer_3_out, multiplexer_4_out, or_1_out,
       plu_1_mux_select_shift_out, plu_1_outp, plu_1_p_state_shift_out, plu_2_mux_select_shift_out,
       plu_2_outp, plu_2_p_state_shift_out, plu_3_mux_select_shift_out, plu_3_outp, plu_3_p_state_shift_out,
       plu_4_mux_select_shift_out, plu_4_outp, plu_4_p_state_shift_out, undriven, undriven_2, undriven_3,
       undriven_4, undriven_5, undriven_6, undriven_7, undriven_8;

  Demultiplexer #(.enable("false")) demultiplexer_1 (
    .out0(demultiplexer_1_out0), .out1(demultiplexer_1_out1), .in(undriven), .sel(or_1_out));
  Multiplexer #(.enable("false")) multiplexer_1 (
    .in0(plu_2_mux_select_shift_out), .in1(plu_2_outp), .out(multiplexer_1_out), .sel(or_1_out));
  Demultiplexer #(.enable("false")) demultiplexer_2 (
    .out0(demultiplexer_2_out0), .out1(demultiplexer_2_out1), .in(undriven_2), .sel(or_1_out));
  Multiplexer #(.enable("false")) multiplexer_2 (
    .in0(undriven_4), .in1(plu_2_outp), .out(multiplexer_2_out), .sel(or_1_out));
  or or_1 (or_1_out, Normal_Test, \config );
  PLU plu_1 (
    .mux_select_shift_in(demultiplexer_1_out0), .inp2(demultiplexer_2_out0), .inp1(demultiplexer_1_out1),
    .p_state_shift_in(plu_2_p_state_shift_out), .mux_select_shift_out(plu_1_mux_select_shift_out),
    .outp(plu_1_outp), .p_state_shift_out(plu_1_p_state_shift_out), .\config (\config ), .test(Normal_Test),
    .lut_shift_in(demultiplexer_2_out1), .lut_shift_out(undriven_3), .clk(clk), .reset(reset));
  PLU plu_2 (
    .mux_select_shift_in(plu_4_mux_select_shift_out), .inp2(plu_1_outp), .inp1(plu_4_outp),
    .p_state_shift_in(plu_4_p_state_shift_out), .mux_select_shift_out(plu_2_mux_select_shift_out),
    .outp(plu_2_outp), .p_state_shift_out(plu_2_p_state_shift_out), .\config (\config ), .test(Normal_Test),
    .lut_shift_in(undriven_3), .lut_shift_out(undriven_4), .clk(clk), .reset(reset));
  Demultiplexer #(.enable("false")) demultiplexer_3 (
    .out0(demultiplexer_3_out0), .out1(demultiplexer_3_out1), .in(undriven_5), .sel(or_1_out));
  Multiplexer #(.enable("false")) multiplexer_3 (
    .in0(undriven_7), .in1(plu_3_outp), .out(multiplexer_3_out), .sel(or_1_out));
  PLU plu_3 (
    .mux_select_shift_in(plu_1_mux_select_shift_out), .inp2(plu_1_outp), .inp1(plu_4_outp),
    .p_state_shift_in(plu_1_p_state_shift_out), .mux_select_shift_out(plu_3_mux_select_shift_out),
    .outp(plu_3_outp), .p_state_shift_out(plu_3_p_state_shift_out), .\config (\config ), .test(Normal_Test),
    .lut_shift_in(undriven_6), .lut_shift_out(undriven_7), .clk(clk), .reset(reset));
  PLU plu_4 (
    .mux_select_shift_in(plu_3_mux_select_shift_out), .inp2(demultiplexer_4_out0),
    .inp1(demultiplexer_3_out0), .p_state_shift_in(demultiplexer_4_out1),
    .mux_select_shift_out(plu_4_mux_select_shift_out), .outp(plu_4_outp),
    .p_state_shift_out(plu_4_p_state_shift_out), .\config (\config ), .test(Normal_Test),
    .lut_shift_in(demultiplexer_3_out1), .lut_shift_out(undriven_6), .clk(clk), .reset(reset));
  Multiplexer #(.enable("false")) multiplexer_4 (
    .in0(plu_3_outp), .in1(plu_3_p_state_shift_out), .out(multiplexer_4_out), .sel(or_1_out));
  Demultiplexer #(.enable("false")) demultiplexer_4 (
    .out0(demultiplexer_4_out0), .out1(demultiplexer_4_out1), .in(undriven_8), .sel(or_1_out));
endmodule

module LUT (
  input  lut_shift_in,
  input  ld,
  input  inp2,
  input  inp1,
  input  Reset,
  input  Clk,
  input  lut_shift_out,
  output outp
);

  wire d_ff_1_q, d_ff_2_q, d_ff_3_q, multiplexer_1_out, multiplexer_2_out;

  D_Flip_Flop d_ff_1 (.clk(Clk), .D(lut_shift_in), .Q(d_ff_1_q), .en(ld), .reset(Reset));  // open: Qn, preset
  D_Flip_Flop d_ff_2 (.clk(Clk), .D(d_ff_1_q), .Q(d_ff_2_q), .en(ld), .reset(Reset));  // open: Qn, preset
  D_Flip_Flop d_ff_3 (.clk(Clk), .D(d_ff_2_q), .Q(d_ff_3_q), .en(ld), .reset(Reset));  // open: Qn, preset
  D_Flip_Flop d_ff_4 (.clk(Clk), .D(d_ff_3_q), .Q(lut_shift_out), .en(ld), .reset(Reset));  // open: Qn, preset
  Multiplexer #(.enable("false")) multiplexer_1 (.in0(d_ff_1_q), .in1(d_ff_2_q), .out(multiplexer_1_out), .sel(inp2));
  Multiplexer #(.enable("false")) multiplexer_2 (
    .in0(d_ff_3_q), .in1(lut_shift_out), .out(multiplexer_2_out), .sel(inp2));
  Multiplexer #(.enable("false")) multiplexer_3 (
    .in0(multiplexer_1_out), .in1(multiplexer_2_out), .out(outp), .sel(inp1));
endmodule

module PLU (
  input  \config ,
  input  test,
  input  lut_shift_in,
  input  mux_select_shift_in,
  input  inp2,
  input  inp1,
  input  p_state_shift_in,
  input  lut_shift_out,
  input  clk,
  input  reset,
  output mux_select_shift_out,
  output outp,
  output p_state_shift_out
);

  wire d_ff_1_q, lut_1_outp, multiplexer_1_out, multiplexer_2_out, not_1_out, not_2_out, or_1_out, or_2_out;

  or or_1 (or_1_out, \config , test);
  LUT lut_1 (
    .ld(or_1_out), .inp2(inp2), .inp1(inp1), .Reset(reset), .outp(lut_1_outp), .lut_shift_in(lut_shift_in),
    .Clk(clk), .lut_shift_out(lut_shift_out));
  D_Flip_Flop d_ff_1 (
    .clk(clk), .D(mux_select_shift_in), .Q(d_ff_1_q), .en(or_1_out), .reset(reset));  // open: Qn, preset
  Multiplexer #(.enable("false")) multiplexer_1 (
    .in0(lut_1_outp), .in1(p_state_shift_in), .out(multiplexer_1_out), .sel(test));
  Multiplexer #(.enable("false")) multiplexer_2 (.in0(inp1), .in1(inp2), .out(multiplexer_2_out), .sel(d_ff_1_q));
  not not_1 (not_1_out, lut_1_outp);
  not not_2 (not_2_out, multiplexer_2_out);
  D_Flip_Flop d_ff_2 (
    .clk(clk), .D(d_ff_1_q), .Q(mux_select_shift_out), .en(or_1_out), .reset(reset));  // open: Qn, preset
  D_Flip_Flop d_ff_3 (
    .clk(clk), .D(multiplexer_1_out), .Q(p_state_shift_out), .en(or_2_out), .reset(reset));  // open: Qn, preset
  or or_2 (or_2_out, not_2_out, test);
  Multiplexer #(.enable("false")) multiplexer_3 (
    .in0(not_1_out), .in1(p_state_shift_out), .out(outp), .sel(mux_select_shift_out));
endmodule
